// Logisim project Multiplexer.circ as structural Verilog: 1 circuit, main circuit main
module main (
  input  [1:0] in_1,
  input  [1:0] in_2,
  input  [1:0] in_3,
  input  [1:0] in_4,
  input  [1:0] in_5,
  input  [1:0] in_6,
  input  [1:0] in_7,
  input  [1:0] in_8,
  input  [3:0] in_9,
  input  [2:0] in_10,
  output [1:0] out_11
);

  wire [1:0] multiplexer_1_out, undriven;

  Multiplexer #(.select(2), .width(2)) multiplexer_1 (
    .in0(in_5), .in1(in_6), .in2(in_7), .in3(in_8), .out(multiplexer_1_out), .sel(undriven));  // open: en
  Multiplexer #(.select(2), .width(2)) multiplexer_2 (
    .in0(in_1), .in1(in_2), .in2(in_3), .in3(in_4), .out(out_11), .sel(multiplexer_1_out));  // open: en
  Multiplexer #(.select(3)) multiplexer_3 ();  // open: in0, in1, in2, in3, in4, in5, in6, in7, out, sel, en
  Multiplexer #(.select(3)) multiplexer_4 ();  // open: in0, in1, in2, in3, in4, in5, in6, in7, out, sel, en
  Multiplexer #(.select(3)) multiplexer_5 ();  // open: in0, in1, in2, in3, in4, in5, in6, in7, out, sel, en
  Multiplexer #(.select(3)) multiplexer_6 ();  // open: in0, in1, in2, in3, in4, in5, in6, in7, out, sel, en
endmodule
