// Logisim project Pipelined CPU.circ as structural Verilog: 1 circuit, main circuit main
module main (
  input  in_1,
  output halt
);

  wire A_Load, ALU_Out_Ld, ALU_Src1, B_Load, clock_1_out, extend, FIR_Load, I_Or_D, imm_backup_ld, IR_Load,
       main_1_zero, Mdr_Ld, Mem2Reg, Mem_Read, Mem_Write, PC_Load, PC_Src, Reg_Src_2, Reg_write, sub;
  wire [1:0] ALU_Src2, Width;
  wire [2:0] ALU_Op_out;
  wire [4:0] rd, rs1, rs2;
  wire [31:0] ALU_Out, main_1_inst, main_2_imm;

  Clock clock_1 (.out(clock_1_out));
  Pipelined_Datapath_main main_1 (
    .pcsrc(PC_Src), .PCLoad(PC_Load), .IOrD(I_Or_D), .RegWrite(Reg_write), .AluOutLd(ALU_Out_Ld), .Rs2(rs2),
    .Rd(rd), .MemRd(Mem_Read), .MemWr(Mem_Write), .Imm(main_2_imm), .imm_backup_ld(imm_backup_ld),
    .Width(Width), .Extend(extend), .clear(in_1), .Clk(clock_1_out), .ALoad(A_Load), .BLoad(B_Load),
    .IRLoad(IR_Load), .MDRLoad(Mdr_Ld), .FIRLoad(FIR_Load), .Mem2Reg(Mem2Reg), .RegSrc2(Reg_Src_2),
    .Rs1(rs1), .ALUSrc1(ALU_Src1), .ALUSrc2(ALU_Src2), .Carry_In(in_1), .SUB(sub), .OP(ALU_Op_out),
    .ALUOut(ALU_Out), .Zero(main_1_zero), .inst(main_1_inst));  // open: Carry_Out
  Pipelined_Control_Unit_main main_2 (
    .ALU_Src1(ALU_Src1), .ALU_Src2(ALU_Src2), .alu_out(ALU_Out), .PC_Src(PC_Src), .ALU_Op(ALU_Op_out),
    .clk(clock_1_out), .Sub(sub), .I_Or_D(I_Or_D), .Mem_Read(Mem_Read), .inst_in(main_1_inst),
    .IR_Load(IR_Load), .imm(main_2_imm), .ALU_Out_Ld(ALU_Out_Ld), .A_Load(A_Load), .B_Load(B_Load),
    .c_in(in_1), .imm_backup_ld(imm_backup_ld), .rs1(rs1), .rs2(rs2), .FIR_Load(FIR_Load),
    .z_in(main_1_zero), .rd(rd), .Mem2Reg(Mem2Reg), .Reg_Write(Reg_write), .Reg_Src_2(Reg_Src_2),
    .PC_Load(PC_Load), .mdr_load(Mdr_Ld), .Mem_Write(Mem_Write), .Sub_in(in_1), .Width(Width),
    .extend(extend), .halt(halt));
endmodule
