// Logisim project Pipelined Control Unit.circ as structural Verilog: 1 circuit, main circuit main
module main (
  input  [31:0] alu_out,
  input  clk,
  input  [31:0] inst_in,
  input  c_in,
  input  z_in,
  input  Sub_in,
  output ALU_Src1,
  output [1:0] ALU_Src2,
  output PC_Src,
  output [2:0] ALU_Op,
  output Sub,
  output I_Or_D,
  output Mem_Read,
  output IR_Load,
  output [31:0] imm,
  output ALU_Out_Ld,
  output A_Load,
  output B_Load,
  output imm_backup_ld,
  output [4:0] rs1,
  output [4:0] rs2,
  output FIR_Load,
  output [4:0] rd,
  output Mem2Reg,
  output Reg_Write,
  output Reg_Src_2,
  output PC_Load,
  output mdr_load,
  output Mem_Write,
  output [1:0] Width,
  output extend,
  output halt
);

  wire and_5_out, and_10_out, and_24_out, and_25_out, and_26_out, and_27_out, and_28_out, and_29_out,
       and_30_out, and_31_out, and_32_out, and_33_out, and_34_out, and_35_out, and_36_out, and_37_out,
       and_38_out, and_39_out, and_40_out, and_41_out, and_42_out, and_43_out, and_44_out, and_45_out,
       and_46_out, and_47_out, and_48_out, and_49_out, and_50_out, and_51_out, and_52_out, and_53_out, AUIPC,
       BRANCH, branch_z, Decode, decoder_1_out0, decoder_1_out1, decoder_1_out4, decoder_1_out5,
       decoder_1_out6, decoder_1_out7, decoder_2_out0, decoder_2_out4, decoder_2_out6, decoder_3_out0,
       decoder_3_out1, decoder_3_out3, decoder_4_out0, decoder_4_out1, decoder_4_out3, decoder_4_out4,
       decoder_4_out5, decoder_5_out0, decoder_5_out1, decoder_5_out2, decoder_5_out3, decoder_5_out4,
       Enable_Custom_OP, I_Type, JAL, JALR, LOAD, LUI, MISC_MEM, multiplexer_16_out, multiplexer_18_out,
       multiplexer_28_out, nor_1_out, OP, OP_IMM, or_1_out, or_2_out, or_3_out, or_5_out, or_12_out,
       or_13_out, or_14_out, or_15_out, or_16_out, or_17_out, or_18_out, or_19_out, or_20_out, RegWrite,
       STORE, SYSTEM, tty_write, U_Type, undriven, undriven_2, undriven_3, undriven_4, undriven_5,
       undriven_6, undriven_7, undriven_8, undriven_9, undriven_10, undriven_11, undriven_12, undriven_13,
       undriven_14, undriven_15, valid_opc, xor_1_out, z, z_enable;
  wire [1:0] bit_extender_14_out, bit_extender_19_out, bit_extender_20_out, bit_extender_21_out,
       multiplexer_10_out, multiplexer_12_out, multiplexer_14_out, multiplexer_19_out, multiplexer_21_out,
       multiplexer_23_out, multiplexer_26_out, multiplexer_27_out, multiplexer_29_out, multiplexer_30_out;
  wire [2:0] and_1_out, and_2_out, and_3_out, bit_extender_1_out, bit_extender_2_out, bit_extender_3_out,
       bit_extender_15_out, bit_extender_17_out, bit_extender_18_out, bit_extender_22_out,
       bit_extender_23_out, bit_extender_24_out, branch_type, counter_1_q, Custom_ALU_OP, multiplexer_13_out,
       multiplexer_15_out, multiplexer_17_out, multiplexer_22_out, multiplexer_24_out, multiplexer_25_out,
       multiplexer_31_out, multiplexer_34_out;
  wire [4:0] multiplexer_3_out, multiplexer_4_out, multiplexer_5_out, multiplexer_11_out, multiplexer_20_out,
       multiplexer_32_out, rd_out, rs1_out, rs2_out;
  wire [6:0] multiplexer_33_out, tty_input;
  wire [19:0] and_4_out, and_6_out, and_7_out, and_8_out, and_9_out, bit_extender_4_out, bit_extender_5_out,
       bit_extender_6_out, bit_extender_7_out, bit_extender_8_out, imm_i, imm_s, imm_sb, or_7_out, or_9_out;
  wire [30:0] bit_extender_10_out;
  wire [30:30] immb;
  wire [31:0] bit_extender_9_out, bit_extender_16_out, imm_out, multiplexer_9_out;

  Pull_Resistor pull_resistor_1 (.node(Mem_Write));
  assign rs1 = inst_in[19:15];  // Buffer buffer_1, 5 bits wide
  Decoder #(.select(3), .enable("false")) decoder_1 (
    .out0(decoder_1_out0), .out1(decoder_1_out1), .out4(decoder_1_out4), .out5(decoder_1_out5),
    .out6(decoder_1_out6), .out7(decoder_1_out7), .sel(inst_in[14:12]));  // open: out2, out3
  Decoder #(.select(3), .enable("false")) decoder_2 (
    .out0(decoder_2_out0), .out4(decoder_2_out4), .out6(decoder_2_out6), .sel(inst_in[14:12]));  // open: out1, out2, out3, out5, out7
  Pull_Resistor pull_resistor_2 (.node(tty_input));
  TTY tty_1 (.data(tty_input), .clk(clk), .we(tty_write));  // open: clr
  Pull_Resistor pull_resistor_3 (.node(tty_write));
  Pull_Resistor pull_resistor_4 (.node(ALU_Src1));
  Pull_Resistor pull_resistor_5 (.node(ALU_Src2));
  Pull_Resistor pull_resistor_6 (.node(PC_Src));
  Pull_Resistor pull_resistor_7 (.node(Sub));
  Pull_Resistor pull_resistor_8 (.node(I_Or_D));
  Pull_Resistor pull_resistor_9 (.node(Mem_Read));
  Pull_Resistor pull_resistor_10 (.node(IR_Load));
  Pull_Resistor pull_resistor_11 (.node(ALU_Out_Ld));
  Pull_Resistor pull_resistor_12 (.node(A_Load));
  Pull_Resistor pull_resistor_13 (.node(B_Load));
  Pull_Resistor pull_resistor_14 (.node(rs1));
  Pull_Resistor pull_resistor_15 (.node(Mem2Reg));
  Pull_Resistor pull_resistor_16 (.node(Reg_Write));
  Pull_Resistor pull_resistor_17 (.node(Reg_Src_2));
  Pull_Resistor pull_resistor_18 (.node(PC_Load));
  Pull_Resistor pull_resistor_19 (.node(mdr_load));
  Pull_Resistor pull_resistor_20 (.node(Sub_in));
  Pull_Resistor pull_resistor_21 (.node(Width));
  Pull_Resistor pull_resistor_22 (.node(extend));
  or or_1 (or_1_out, decoder_1_out0, decoder_1_out1);
  assign bit_extender_1_out = {{2{or_1_out}}, or_1_out};  // Bit_Extender bit_extender_1
  assign bit_extender_2_out = {{2{or_2_out}}, or_2_out};  // Bit_Extender bit_extender_2
  or or_2 (or_2_out, decoder_1_out4, decoder_1_out5);
  assign bit_extender_3_out = {{2{or_3_out}}, or_3_out};  // Bit_Extender bit_extender_3
  or or_3 (or_3_out, decoder_1_out6, decoder_1_out7);
  or or_4 (branch_z, decoder_2_out0, decoder_2_out4, decoder_2_out6);
  assign bit_extender_4_out = {{19{BRANCH}}, BRANCH};  // Bit_Extender bit_extender_4
  assign and_1_out = bit_extender_1_out & 3'b100;  // AND_Gate and_1, 3 bits wide
  assign and_2_out = bit_extender_2_out & 3'b010;  // AND_Gate and_2, 3 bits wide
  assign and_3_out = bit_extender_3_out & 3'b011;  // AND_Gate and_3, 3 bits wide
  or or_5 (or_5_out, AUIPC, LUI);
  assign bit_extender_5_out = {{19{or_5_out}}, or_5_out};  // Bit_Extender bit_extender_5
  assign bit_extender_6_out = {{19{STORE}}, STORE};  // Bit_Extender bit_extender_6
  assign bit_extender_7_out = {{19{I_Type}}, I_Type};  // Bit_Extender bit_extender_7
  assign bit_extender_8_out = {{19{JAL}}, JAL};  // Bit_Extender bit_extender_8
  assign and_4_out = imm_sb & bit_extender_4_out;  // AND_Gate and_4, 20 bits wide
  and and_5 (and_5_out, inst_in[12], ~inst_in[13], inst_in[14]);  // AND_Gate
  Pull_Resistor pull_resistor_23 (.node(imm_backup_ld));
  Pull_Resistor pull_resistor_24 (.node(FIR_Load));
  assign branch_type = and_1_out | and_2_out | and_3_out;  // OR_Gate or_6, 3 bits wide
  assign and_6_out = inst_in[31:12] & bit_extender_5_out;  // AND_Gate and_6, 20 bits wide
  assign and_7_out = imm_s & bit_extender_6_out;  // AND_Gate and_7, 20 bits wide
  assign and_8_out = imm_i & bit_extender_7_out;  // AND_Gate and_8, 20 bits wide
  assign and_9_out = {inst_in[31], inst_in[19:12], inst_in[20], inst_in[30:21]} & bit_extender_8_out;  // AND_Gate and_9, 20 bits wide
  assign or_7_out = and_9_out | and_4_out;  // OR_Gate or_7, 20 bits wide
  Pull_Resistor pull_resistor_25 ();  // open: node
  D_Flip_Flop d_ff_1 (.clk(clk), .D(z_in), .Q(z), .en(z_enable));  // open: Qn, preset, reset
  Pull_Resistor pull_resistor_26 (.node(z_enable));
  or or_8 (I_Type, LOAD, JALR, OP_IMM);
  assign bit_extender_9_out = {{12{or_9_out[19]}}, or_9_out};  // Bit_Extender bit_extender_9
  assign or_9_out = and_6_out | and_7_out | and_8_out;  // OR_Gate or_9, 20 bits wide
  assign bit_extender_10_out = {{11{or_7_out[19]}}, or_7_out};  // Bit_Extender bit_extender_10
  and and_10 (and_10_out, inst_in[30], and_5_out, I_Type);
  and and_11 (valid_opc, inst_in[0], inst_in[1]);
  Decoder #(.select(2), .disabled(0)) decoder_3 (
    .out0(decoder_3_out0), .out1(decoder_3_out1), .out3(decoder_3_out3), .sel(inst_in[6:5]), .en(valid_opc));  // open: out2
  Multiplexer #(.enable("false")) multiplexer_1 (.in0(immb[30]), .in1(1'b0), .out(imm[30]), .sel(and_10_out));
  and and_12 (LOAD, decoder_3_out0, decoder_4_out0);
  and and_13 (STORE, decoder_3_out1, decoder_4_out0);
  and and_14 (BRANCH, decoder_3_out3, decoder_4_out0);
  nor nor_1 (nor_1_out, MISC_MEM, LOAD, OP_IMM, AUIPC, STORE, OP, LUI, BRANCH, JALR, JAL, SYSTEM);
  assign {imm[31], immb[30], imm[29:0]} = bit_extender_9_out | {bit_extender_10_out, 1'b0};  // OR_Gate or_10, 32 bits wide
  Decoder #(.select(3), .disabled(0)) decoder_4 (
    .out0(decoder_4_out0), .out1(decoder_4_out1), .out3(decoder_4_out3), .out4(decoder_4_out4),
    .out5(decoder_4_out5), .sel(inst_in[4:2]), .en(valid_opc));  // open: out2, out6, out7
  and and_15 (MISC_MEM, decoder_3_out0, decoder_4_out3);
  and and_16 (OP, decoder_3_out1, decoder_4_out4);
  and and_17 (JALR, decoder_4_out1, decoder_3_out3);
  and and_18 (halt, Decode, nor_1_out);
  and and_19 (OP_IMM, decoder_3_out0, decoder_4_out4);
  and and_20 (LUI, decoder_3_out1, decoder_4_out5);
  and and_21 (JAL, decoder_4_out3, decoder_3_out3);
  Multiplexer #(.width(3), .enable("false")) multiplexer_2 (
    .in0(inst_in[14:12]), .in1(Custom_ALU_OP), .out(ALU_Op), .sel(Enable_Custom_OP));
  Pull_Resistor pull_resistor_27 (.node(Enable_Custom_OP));
  and and_22 (AUIPC, decoder_3_out0, decoder_4_out5);
  and and_23 (SYSTEM, decoder_4_out4, decoder_3_out3);
  assign imm_i = {{8{inst_in[31]}}, inst_in[31:20]};  // Bit_Extender bit_extender_11
  assign rs1 = multiplexer_3_out;  // Buffer buffer_2, 5 bits wide
  Pull_Resistor pull_resistor_28 (.node(Custom_ALU_OP[0]));
  Pull_Resistor pull_resistor_29 (.node(Custom_ALU_OP[2]));
  or or_11 (U_Type, AUIPC, LUI);
  assign imm_s = {{8{inst_in[31]}}, {inst_in[31:25], inst_in[11:7]}};  // Bit_Extender bit_extender_12
  assign imm_sb = {{8{inst_in[31]}}, {inst_in[31], inst_in[7], inst_in[30:25], inst_in[11:8]}};  // Bit_Extender bit_extender_13
  and and_24 (and_24_out, decoder_5_out1, SYSTEM);
  buf buffer_3 (A_Load, and_24_out);
  Multiplexer #(.width(5), .enable("false")) multiplexer_3 (
    .in1(5'b01010), .out(multiplexer_3_out), .sel(and_24_out));  // open: in0
  Pull_Resistor pull_resistor_30 (.node(Custom_ALU_OP[1]));
  assign rs1_out = multiplexer_5_out;  // Buffer buffer_4, 5 bits wide
  assign rs2_out = multiplexer_4_out;  // Buffer buffer_5, 5 bits wide
  buf buffer_6 (Decode, decoder_5_out1);
  Bit_Extender #(.in_width(1), .out_width(2)) bit_extender_14 (.out(bit_extender_14_out));  // open: in
  Bit_Extender #(.in_width(1), .out_width(3)) bit_extender_15 (.out(bit_extender_15_out));  // open: in
  or or_12 (or_12_out, LOAD, STORE);
  and and_25 (and_25_out, decoder_5_out1, or_12_out);
  and and_26 (and_26_out, decoder_5_out1, STORE);
  Multiplexer #(.width(5), .enable("false")) multiplexer_4 (
    .in1(inst_in[24:20]), .out(multiplexer_4_out), .sel(and_26_out));  // open: in0
  buf buffer_7 (B_Load, and_26_out);
  buf buffer_8 (ALU_Src1, undriven);
  assign ALU_Src2 = bit_extender_14_out;  // Buffer buffer_9, 2 bits wide
  buf buffer_10 (PC_Src, decoder_5_out0);
  assign ALU_Op = bit_extender_15_out;  // Buffer buffer_11, 3 bits wide
  // Buffer buffer_12 has open pins: in=open, out=Sub
  // Buffer buffer_13 has open pins: in=open, out=PC_Load
  // Buffer buffer_14 has open pins: in=open, out=I_Or_D
  buf buffer_15 (Mem_Read, decoder_5_out0);
  buf buffer_16 (IR_Load, decoder_5_out0);
  assign imm_out = multiplexer_9_out;  // Buffer buffer_17, 32 bits wide
  assign ALU_Src2 = multiplexer_10_out;  // Buffer buffer_18, 2 bits wide
  assign rs1_out = multiplexer_11_out;  // Buffer buffer_19, 5 bits wide
  or or_13 (or_13_out, LUI, AUIPC);
  and and_27 (and_27_out, decoder_5_out1, or_13_out);
  buf buffer_20 (A_Load, and_27_out);
  buf buffer_21 (A_Load, and_25_out);
  Multiplexer #(.width(5), .enable("false")) multiplexer_5 (
    .in1(rs1), .out(multiplexer_5_out), .sel(and_25_out));  // open: in0
  Decoder #(.select(3), .enable("false")) decoder_5 (
    .out0(decoder_5_out0), .out1(decoder_5_out1), .out2(decoder_5_out2), .out3(decoder_5_out3),
    .out4(decoder_5_out4), .sel(counter_1_q));  // open: out5, out6, out7
  Counter #(.width(3), .max('h4), .trigger("falling")) counter_1 (
    .Q(counter_1_q), .clk(clk));  // open: load, D, count, carry, clr
  or or_14 (or_14_out, OP, I_Type);
  and and_28 (and_28_out, decoder_5_out1, or_14_out);
  Multiplexer #(.width(5), .enable("false")) multiplexer_6 (.in1(rs1), .out(rs1_out), .sel(and_28_out));  // open: in0
  Multiplexer #(.width(5), .enable("false")) multiplexer_7 (
    .in1(inst_in[24:20]), .out(rs2_out), .sel(and_28_out));  // open: in0
  Multiplexer #(.width(5), .enable("false")) multiplexer_8 (
    .in1(inst_in[11:7]), .out(rd_out), .sel(and_28_out));  // open: in0
  Multiplexer #(.width(32), .enable("false")) multiplexer_9 (
    .in1(imm), .out(multiplexer_9_out), .sel(and_28_out));  // open: in0
  and and_29 (and_29_out, decoder_5_out1, JAL);
  and and_30 (and_30_out, decoder_5_out1, JALR);
  and and_31 (and_31_out, decoder_5_out1, BRANCH);
  assign ALU_Src2 = multiplexer_12_out;  // Buffer buffer_22, 2 bits wide
  buf buffer_23 (imm_backup_ld, decoder_5_out1);
  // Buffer buffer_24 has open pins: in=open, out=Reg_Write
  buf buffer_25 (A_Load, and_28_out);
  buf buffer_26 (B_Load, and_28_out);
  // Buffer buffer_27 has open pins: in=open, out=Reg_Src_2
  // Buffer buffer_28 has open pins: in=open, out=ALU_Src1
  Multiplexer #(.width(2), .enable("false")) multiplexer_10 (
    .in1(2'b10), .out(multiplexer_10_out), .sel(and_29_out));  // open: in0
  buf buffer_29 (Sub, undriven_7);
  buf buffer_30 (ALU_Out_Ld, and_29_out);
  Multiplexer #(.width(5), .enable("false")) multiplexer_11 (
    .in1(rs1), .out(multiplexer_11_out), .sel(and_30_out));  // open: in0
  buf buffer_31 (A_Load, and_30_out);
  Multiplexer #(.width(2), .enable("false")) multiplexer_12 (
    .in1(2'b10), .out(multiplexer_12_out), .sel(and_31_out));  // open: in0
  // Buffer buffer_32 has open pins: in=open, out=ALU_Src1
  buf buffer_33 (Sub, undriven_4);
  buf buffer_34 (ALU_Out_Ld, and_31_out);
  buf buffer_35 (A_Load, and_31_out);
  buf buffer_36 (B_Load, and_31_out);
  buf buffer_37 (Enable_Custom_OP, and_31_out);
  assign Custom_ALU_OP = multiplexer_13_out;  // Buffer buffer_38, 3 bits wide
  Multiplexer #(.width(3), .enable("false")) multiplexer_13 (
    .in1(3'b000), .out(multiplexer_13_out), .sel(and_31_out));  // open: in0
  and and_32 (and_32_out, decoder_5_out2, SYSTEM);
  assign ALU_Src2 = multiplexer_14_out;  // Buffer buffer_39, 2 bits wide
  Multiplexer #(.width(2), .enable("false")) multiplexer_14 (
    .in1(2'b10), .out(multiplexer_14_out), .sel(and_32_out));  // open: in0
  buf buffer_40 (FIR_Load, decoder_5_out1);
  buf buffer_41 (PC_Load, undriven_2);
  buf buffer_42 (PC_Src, undriven_2);
  assign bit_extender_16_out = {{31{1'b0}}, undriven_5};  // Bit_Extender bit_extender_16
  assign imm_out = bit_extender_16_out;  // Buffer buffer_43, 32 bits wide
  assign bit_extender_17_out = {{2{1'b0}}, undriven_6};  // Bit_Extender bit_extender_17
  assign ALU_Op = bit_extender_17_out;  // Buffer buffer_44, 3 bits wide
  assign rd_out = multiplexer_20_out;  // Buffer buffer_45, 5 bits wide
  assign ALU_Op = bit_extender_18_out;  // Buffer buffer_46, 3 bits wide
  assign bit_extender_18_out = {{2{1'b0}}, undriven_3};  // Bit_Extender bit_extender_18
  buf buffer_47 (ALU_Out_Ld, and_32_out);
  buf buffer_48 (ALU_Src1, and_32_out);
  buf buffer_49 (PC_Load, undriven_8);
  buf buffer_50 (PC_Src, undriven_8);
  and and_33 (and_33_out, decoder_5_out2, OP);
  and and_34 (and_34_out, decoder_5_out2, I_Type);
  assign ALU_Src2 = multiplexer_19_out;  // Buffer buffer_51, 2 bits wide
  and and_35 (and_35_out, decoder_5_out2, JAL);
  and and_36 (and_36_out, decoder_5_out2, LUI);
  and and_37 (and_37_out, decoder_5_out2, BRANCH);
  Multiplexer #(.width(3), .enable("false")) multiplexer_15 (
    .in1(inst_in[14:12]), .out(multiplexer_15_out), .sel(and_33_out));  // open: in0
  Multiplexer #(.enable("false")) multiplexer_16 (
    .in1(Sub_in), .out(multiplexer_16_out), .sel(and_33_out));  // open: in0
  // Buffer buffer_52 has open pins: in=open, out=ALU_Out_Ld
  buf buffer_53 (ALU_Src1, and_33_out);
  assign bit_extender_19_out = {{1{1'b0}}, and_33_out};  // Bit_Extender bit_extender_19
  Multiplexer #(.width(3), .enable("false")) multiplexer_17 (
    .in1(inst_in[14:12]), .out(multiplexer_17_out), .sel(and_34_out));  // open: in0
  Multiplexer #(.enable("false")) multiplexer_18 (
    .in1(Sub_in), .out(multiplexer_18_out), .sel(and_34_out));  // open: in0
  buf buffer_54 (ALU_Out_Ld, and_34_out);
  buf buffer_55 (ALU_Src1, and_34_out);
  Multiplexer #(.width(2), .enable("false")) multiplexer_19 (
    .in1(2'b10), .out(multiplexer_19_out), .sel(and_34_out));  // open: in0
  // Buffer buffer_56 has open pins: in=open, out=Mem2Reg
  Multiplexer #(.width(5), .enable("false")) multiplexer_20 (
    .in1(inst_in[11:7]), .out(multiplexer_20_out), .sel(and_35_out));  // open: in0
  buf buffer_57 (Reg_Write, and_35_out);
  buf buffer_58 (ALU_Src1, and_36_out);
  buf buffer_59 (ALU_Out_Ld, and_36_out);
  Multiplexer #(.width(2), .enable("false")) multiplexer_21 (
    .in1(2'b10), .out(multiplexer_21_out), .sel(and_36_out));  // open: in0
  Multiplexer #(.width(3), .enable("false")) multiplexer_22 (
    .in1(3'b000), .out(multiplexer_22_out), .sel(and_36_out));  // open: in0
  and and_38 (and_38_out, decoder_5_out2, AUIPC);
  Multiplexer #(.width(2), .enable("false")) multiplexer_23 (
    .in1(2'b10), .out(multiplexer_23_out), .sel(and_38_out));  // open: in0
  buf buffer_60 (ALU_Out_Ld, and_38_out);
  buf buffer_61 (Enable_Custom_OP, and_38_out);
  Multiplexer #(.width(3), .enable("false")) multiplexer_24 (
    .in1(3'b000), .out(multiplexer_24_out), .sel(and_38_out));  // open: in0
  assign Custom_ALU_OP = multiplexer_24_out;  // Buffer buffer_62, 3 bits wide
  or or_15 (or_15_out, LOAD, STORE);
  and and_39 (and_39_out, decoder_5_out2, or_15_out);
  buf buffer_63 (ALU_Out_Ld, and_39_out);
  buf buffer_64 (ALU_Src1, and_39_out);
  Multiplexer #(.width(3), .enable("false")) multiplexer_25 (
    .in1(branch_type), .out(multiplexer_25_out), .sel(and_37_out));  // open: in0
  buf buffer_65 (Sub, and_37_out);
  buf buffer_66 (ALU_Src1, and_37_out);
  buf buffer_67 (z_enable, and_37_out);
  assign bit_extender_20_out = {{1{1'b0}}, and_37_out};  // Bit_Extender bit_extender_20
  buf buffer_68 (PC_Load, undriven_9);
  assign ALU_Op = multiplexer_15_out;  // Buffer buffer_69, 3 bits wide
  buf buffer_70 (Sub, multiplexer_16_out);
  assign ALU_Src2 = bit_extender_19_out;  // Buffer buffer_71, 2 bits wide
  assign ALU_Op = multiplexer_17_out;  // Buffer buffer_72, 3 bits wide
  buf buffer_73 (Sub, multiplexer_18_out);
  assign ALU_Src2 = multiplexer_21_out;  // Buffer buffer_74, 2 bits wide
  buf buffer_75 (Enable_Custom_OP, and_36_out);
  assign Custom_ALU_OP = multiplexer_22_out;  // Buffer buffer_76, 3 bits wide
  assign bit_extender_21_out = {{1{1'b0}}, and_39_out};  // Bit_Extender bit_extender_21
  assign ALU_Src2 = bit_extender_21_out;  // Buffer buffer_77, 2 bits wide
  assign ALU_Op = bit_extender_22_out;  // Buffer buffer_78, 3 bits wide
  assign bit_extender_22_out = {{2{1'b0}}, undriven_10};  // Bit_Extender bit_extender_22
  buf buffer_79 (Sub, undriven_11);
  buf buffer_80 (Enable_Custom_OP, and_37_out);
  assign Custom_ALU_OP = multiplexer_25_out;  // Buffer buffer_81, 3 bits wide
  assign ALU_Src2 = bit_extender_20_out;  // Buffer buffer_82, 2 bits wide
  buf buffer_83 (PC_Src, undriven_9);
  assign ALU_Src2 = multiplexer_26_out;  // Buffer buffer_84, 2 bits wide
  assign ALU_Src2 = multiplexer_23_out;  // Buffer buffer_85, 2 bits wide
  and and_40 (and_40_out, decoder_5_out3, JAL);
  assign ALU_Src2 = multiplexer_27_out;  // Buffer buffer_86, 2 bits wide
  and and_41 (and_41_out, decoder_5_out3, JALR);
  Multiplexer #(.width(2), .enable("false")) multiplexer_26 (
    .in1(2'b10), .out(multiplexer_26_out), .sel(and_41_out));  // open: in0
  and and_42 (and_42_out, decoder_5_out3, LOAD);
  and and_43 (and_43_out, decoder_5_out3, STORE);
  Multiplexer #(.width(2), .enable("false")) multiplexer_27 (
    .in1(2'b10), .out(multiplexer_27_out), .sel(and_40_out));  // open: in0
  // Buffer buffer_87 has open pins: in=open, out=ALU_Src1
  // NOT_Gate not_1 is placed but not wired
  Bit_Extender #(.in_width(1), .out_width(3)) bit_extender_23 (.out(bit_extender_23_out));  // open: in
  buf buffer_88 (Sub, undriven_13);
  buf buffer_89 (ALU_Out_Ld, and_40_out);
  buf buffer_90 (ALU_Src1, and_41_out);
  assign ALU_Op = bit_extender_24_out;  // Buffer buffer_91, 3 bits wide
  Bit_Extender #(.in_width(1), .out_width(3)) bit_extender_24 (.out(bit_extender_24_out));  // open: in
  buf buffer_92 (Sub, undriven_12);
  buf buffer_93 (ALU_Out_Ld, and_41_out);
  buf buffer_94 (Mem_Read, and_42_out);
  buf buffer_95 (mdr_load, and_42_out);
  buf buffer_96 (I_Or_D, and_42_out);
  buf buffer_97 (extend, multiplexer_28_out);
  Multiplexer #(.enable("false")) multiplexer_28 (
    .in1(inst_in[14]), .out(multiplexer_28_out), .sel(and_42_out));  // open: in0
  Multiplexer #(.width(2), .enable("false")) multiplexer_29 (
    .in1(inst_in[13:12]), .out(multiplexer_29_out), .sel(and_42_out));  // open: in0
  buf buffer_98 (Mem_Write, and_43_out);
  buf buffer_99 (I_Or_D, and_43_out);
  // Buffer buffer_100 has open pins: in=open, out=extend
  Multiplexer #(.width(2), .enable("false")) multiplexer_30 (
    .in1(inst_in[13:12]), .out(multiplexer_30_out), .sel(and_43_out));  // open: in0
  or or_16 (or_16_out, OP_IMM, OP);
  and and_44 (and_44_out, decoder_5_out3, or_16_out);
  buf buffer_101 (Reg_Write, and_44_out);
  or or_17 (or_17_out, OP, I_Type);
  and and_45 (and_45_out, decoder_5_out4, or_17_out);
  assign ALU_Op = bit_extender_23_out;  // Buffer buffer_102, 3 bits wide
  and and_46 (and_46_out, decoder_5_out4, or_18_out);
  assign Width = multiplexer_29_out;  // Buffer buffer_103, 2 bits wide
  assign Width = multiplexer_30_out;  // Buffer buffer_104, 2 bits wide
  and and_47 (and_47_out, decoder_5_out3, SYSTEM);
  // Buffer buffer_105 has open pins: in=open, out=PC_Load
  buf buffer_106 (Reg_Write, and_45_out);
  buf buffer_107 (Reg_Src_2, and_45_out);
  or or_18 (or_18_out, JAL, JALR);
  // Buffer buffer_108 has open pins: in=open, out=PC_Src
  // Buffer buffer_109 has open pins: in=open, out=PC_Load
  or or_19 (or_19_out, LUI, AUIPC);
  and and_48 (and_48_out, decoder_5_out4, or_19_out);
  buf buffer_110 (Reg_Write, and_48_out);
  buf buffer_111 (Enable_Custom_OP, and_48_out);
  Multiplexer #(.width(3), .enable("false")) multiplexer_31 (
    .in1(3'b000), .out(multiplexer_31_out), .sel(and_48_out));  // open: in0
  assign Custom_ALU_OP = multiplexer_31_out;  // Buffer buffer_112, 3 bits wide
  or or_20 (or_20_out, LOAD, STORE);
  and and_49 (and_49_out, decoder_5_out4, or_20_out);
  Multiplexer #(.width(5), .enable("false")) multiplexer_32 (
    .in1(inst_in[11:7]), .out(multiplexer_32_out), .sel(and_49_out));  // open: in0
  assign rd_out = multiplexer_32_out;  // Buffer buffer_113, 5 bits wide
  and and_50 (and_50_out, decoder_5_out4, SYSTEM);
  Multiplexer #(.width(7), .enable("false")) multiplexer_33 (
    .in1(alu_out[6:0]), .out(multiplexer_33_out), .sel(and_50_out));  // open: in0
  buf buffer_114 (PC_Src, and_45_out);
  buf buffer_115 (Mem2Reg, and_49_out);
  buf buffer_116 (RegWrite, and_49_out);
  assign tty_input = multiplexer_33_out;  // Buffer buffer_117, 7 bits wide
  buf buffer_118 (PC_Src, and_48_out);
  buf buffer_119 (imm_backup_ld, undriven_14);
  buf buffer_120 (PC_Load, decoder_5_out4);
  Multiplexer #(.width(3), .enable("false")) multiplexer_34 (
    .in1(3'b000), .out(multiplexer_34_out), .sel(decoder_5_out4));  // open: in0
  assign Custom_ALU_OP = multiplexer_34_out;  // Buffer buffer_121, 3 bits wide
  and and_51 (and_51_out, decoder_5_out4, BRANCH);
  and and_52 (and_52_out, decoder_5_out4, SYSTEM);
  buf buffer_122 (Enable_Custom_OP, decoder_5_out4);
  xor xor_1 (xor_1_out, z, branch_z);
  and and_53 (and_53_out, and_51_out, xor_1_out);
  buf buffer_123 (tty_write, and_52_out);
  buf buffer_124 (PC_Load, undriven_15);
  buf buffer_125 (PC_Src, and_53_out);
  buf buffer_126 (PC_Src, and_52_out);

  assign rd = inst_in[11:7];
  assign rs2 = inst_in[24:20];

  // Other names for the same wires on the sheet: inst[31:0] = inst_in; funct7[6:0] = inst_in[31:25];
  //   imm_u[19:0] = inst_in[31:12]; imm_uj[19:0] = {inst_in[31], inst_in[19:12], inst_in[20], inst_in[30:21]};
  //   ALU_Op_out[2:0] = ALU_Op; c = c_in; immb (some bits) = {imm[31], imm[29:0]}; funct3[2:0] = inst_in[14:12];
  //   inst_4_2[2:0] = inst_in[4:2]; inst_6_5[1:0] = inst_in[6:5]; Mdr_Ld = mdr_load; sub_out = Sub

  // Notes on the sheet:
  //   buffer_1 drives only 1 and floats otherwise
  //   buffer_2 drives only 1 and floats otherwise
  //   buffer_3 drives only 1 and floats otherwise
  //   buffer_4 drives only 1 and floats otherwise
  //   buffer_5 drives only 1 and floats otherwise
  //   buffer_7 drives only 1 and floats otherwise
  //   buffer_8 drives only 1 and floats otherwise
  //   buffer_9 drives only 1 and floats otherwise
  //   buffer_10 drives only 1 and floats otherwise
  //   buffer_11 drives only 1 and floats otherwise
  //   buffer_12 drives only 1 and floats otherwise
  //   buffer_13 drives only 1 and floats otherwise
  //   buffer_14 drives only 1 and floats otherwise
  //   buffer_15 drives only 1 and floats otherwise
  //   buffer_16 drives only 1 and floats otherwise
  //   buffer_17 drives only 1 and floats otherwise
  //   buffer_18 drives only 1 and floats otherwise
  //   buffer_19 drives only 1 and floats otherwise
  //   buffer_20 drives only 1 and floats otherwise
  //   buffer_21 drives only 1 and floats otherwise
  //   buffer_22 drives only 1 and floats otherwise
  //   buffer_23 drives only 1 and floats otherwise
  //   buffer_24 drives only 1 and floats otherwise
  //   buffer_25 drives only 1 and floats otherwise
  //   buffer_26 drives only 1 and floats otherwise
  //   buffer_27 drives only 1 and floats otherwise
  //   buffer_28 drives only 1 and floats otherwise
  //   buffer_29 drives only 1 and floats otherwise
  //   buffer_30 drives only 1 and floats otherwise
  //   buffer_31 drives only 1 and floats otherwise
  //   buffer_32 drives only 1 and floats otherwise
  //   buffer_33 drives only 1 and floats otherwise
  //   buffer_34 drives only 1 and floats otherwise
  //   buffer_35 drives only 1 and floats otherwise
  //   buffer_36 drives only 1 and floats otherwise
  //   buffer_37 drives only 1 and floats otherwise
  //   buffer_38 drives only 1 and floats otherwise
  //   buffer_39 drives only 1 and floats otherwise
  //   buffer_40 drives only 1 and floats otherwise
  //   buffer_41 drives only 1 and floats otherwise
  //   buffer_42 drives only 1 and floats otherwise
  //   buffer_43 drives only 1 and floats otherwise
  //   buffer_44 drives only 1 and floats otherwise
  //   buffer_45 drives only 1 and floats otherwise
  //   buffer_46 drives only 1 and floats otherwise
  //   buffer_47 drives only 1 and floats otherwise
  //   buffer_48 drives only 1 and floats otherwise
  //   buffer_49 drives only 1 and floats otherwise
  //   buffer_50 drives only 1 and floats otherwise
  //   buffer_51 drives only 1 and floats otherwise
  //   buffer_52 drives only 1 and floats otherwise
  //   buffer_53 drives only 1 and floats otherwise
  //   buffer_54 drives only 1 and floats otherwise
  //   buffer_55 drives only 1 and floats otherwise
  //   buffer_56 drives only 1 and floats otherwise
  //   buffer_57 drives only 1 and floats otherwise
  //   buffer_58 drives only 1 and floats otherwise
  //   buffer_59 drives only 1 and floats otherwise
  //   buffer_60 drives only 1 and floats otherwise
  //   buffer_61 drives only 1 and floats otherwise
  //   buffer_62 drives only 1 and floats otherwise
  //   buffer_63 drives only 1 and floats otherwise
  //   buffer_64 drives only 1 and floats otherwise
  //   buffer_65 drives only 1 and floats otherwise
  //   buffer_66 drives only 1 and floats otherwise
  //   buffer_67 drives only 1 and floats otherwise
  //   buffer_68 drives only 1 and floats otherwise
  //   buffer_69 drives only 1 and floats otherwise
  //   buffer_70 drives only 1 and floats otherwise
  //   buffer_71 drives only 1 and floats otherwise
  //   buffer_72 drives only 1 and floats otherwise
  //   buffer_73 drives only 1 and floats otherwise
  //   buffer_74 drives only 1 and floats otherwise
  //   buffer_75 drives only 1 and floats otherwise
  //   buffer_76 drives only 1 and floats otherwise
  //   buffer_77 drives only 1 and floats otherwise
  //   buffer_78 drives only 1 and floats otherwise
  //   buffer_79 drives only 1 and floats otherwise
  //   buffer_80 drives only 1 and floats otherwise
  //   buffer_81 drives only 1 and floats otherwise
  //   buffer_82 drives only 1 and floats otherwise
  //   buffer_83 drives only 1 and floats otherwise
  //   buffer_84 drives only 1 and floats otherwise
  //   buffer_85 drives only 1 and floats otherwise
  //   buffer_86 drives only 1 and floats otherwise
  //   buffer_87 drives only 1 and floats otherwise
  //   not_1 drives only 1 and floats otherwise
  //   buffer_88 drives only 1 and floats otherwise
  //   buffer_89 drives only 1 and floats otherwise
  //   buffer_90 drives only 1 and floats otherwise
  //   buffer_91 drives only 1 and floats otherwise
  //   buffer_92 drives only 1 and floats otherwise
  //   buffer_93 drives only 1 and floats otherwise
  //   buffer_94 drives only 1 and floats otherwise
  //   buffer_95 drives only 1 and floats otherwise
  //   buffer_96 drives only 1 and floats otherwise
  //   buffer_97 drives only 1 and floats otherwise
  //   buffer_98 drives only 1 and floats otherwise
  //   buffer_99 drives only 1 and floats otherwise
  //   buffer_100 drives only 1 and floats otherwise
  //   buffer_101 drives only 1 and floats otherwise
  //   buffer_102 drives only 1 and floats otherwise
  //   buffer_103 drives only 1 and floats otherwise
  //   buffer_104 drives only 1 and floats otherwise
  //   buffer_105 drives only 1 and floats otherwise
  //   buffer_106 drives only 1 and floats otherwise
  //   buffer_107 drives only 1 and floats otherwise
  //   buffer_108 drives only 1 and floats otherwise
  //   buffer_109 drives only 1 and floats otherwise
  //   buffer_110 drives only 1 and floats otherwise
  //   buffer_111 drives only 1 and floats otherwise
  //   buffer_112 drives only 1 and floats otherwise
  //   buffer_113 drives only 1 and floats otherwise
  //   buffer_114 drives only 1 and floats otherwise
  //   buffer_115 drives only 1 and floats otherwise
  //   buffer_116 drives only 1 and floats otherwise
  //   buffer_117 drives only 1 and floats otherwise
  //   buffer_118 drives only 1 and floats otherwise
  //   buffer_119 drives only 1 and floats otherwise
  //   buffer_120 drives only 1 and floats otherwise
  //   buffer_121 drives only 1 and floats otherwise
  //   buffer_122 drives only 1 and floats otherwise
  //   buffer_123 drives only 1 and floats otherwise
  //   buffer_124 drives only 1 and floats otherwise
  //   buffer_125 drives only 1 and floats otherwise
  //   buffer_126 drives only 1 and floats otherwise
endmodule
