// Logisim project Pipelined Datapath.circ as structural Verilog: 1 circuit, main circuit main
module main (
  input  Clk,
  input  pcsrc,
  input  PCLoad,
  input  SUB,
  input  IOrD,
  input  Carry_In,
  input  ALoad,
  input  Mem2Reg,
  input  MDRLoad,
  input  ALUSrc1,
  input  BLoad,
  input  RegWrite,
  input  [2:0] OP,
  input  AluOutLd,
  input  [4:0] Rs2,
  input  IRLoad,
  input  [4:0] Rd,
  input  [4:0] Rs1,
  input  RegSrc2,
  input  [1:0] ALUSrc2,
  input  MemRd,
  input  MemWr,
  input  [31:0] Imm,
  input  FIRLoad,
  input  imm_backup_ld,
  input  [1:0] Width,
  input  Extend,
  input  clear,
  output Carry_Out,
  output Zero,
  output [31:0] inst,
  output [31:0] ALUOut
);

  wire alu_2_carry_out, memory_1_p8;
  wire [4:0] multiplexer_4_out;
  wire [31:0] A_q, alu_1_ouput, alu_2_ouput, B, imm_backup_q, main_1_output, main_1_output_2, MDR_q,
       memory_1_p11, multiplexer_1_out, multiplexer_2_out, multiplexer_3_out, multiplexer_5_out,
       multiplexer_6_out, PC_q;

  Multiplexer #(.width(32)) multiplexer_1 (
    .in0(ALUOut), .in1(alu_2_ouput), .out(multiplexer_1_out), .sel(pcsrc));  // open: en
  Register #(.width(32)) PC (.D(multiplexer_1_out), .en(PCLoad), .Q(PC_q), .clk(Clk));  // open: clr
  Multiplexer #(.width(32), .enable("false")) multiplexer_2 (
    .in0(PC_q), .in1(ALUOut), .out(multiplexer_2_out), .sel(IOrD));
  // Memory memory_1: pin names not known; wires that end beside it: multiplexer_2_out, B, MemWr, MemRd, Width, Extend, Clk, memory_1_p8, MemRd, clear, memory_1_p11, FIRLoad, memory_1_p8, inst
  Register #(.width(32)) IR (.D(memory_1_p11), .en(IRLoad), .Q(inst), .clk(memory_1_p8));  // open: clr
  Register #(.width(32)) MDR (.D(memory_1_p11), .en(MDRLoad), .Q(MDR_q), .clk(memory_1_p8));  // open: clr
  Multiplexer #(.width(32), .enable("false")) multiplexer_3 (
    .in0(ALUOut), .in1(MDR_q), .out(multiplexer_3_out), .sel(Mem2Reg));
  Register #(.width(32)) FIR ();  // open: D, en, Q, clk, clr
  Multiplexer #(.width(5), .enable("false")) multiplexer_4 (
    .in0(Rs2), .in1(Rd), .out(multiplexer_4_out), .sel(RegSrc2));
  register_revised_main main_1 (
    .Clock(Clk), .enable(RegWrite), .write_data(multiplexer_3_out), .write_address(Rd),
    .raddr2(multiplexer_4_out), .raddr1(Rs1), .Output(main_1_output), .Output_2(main_1_output_2));
  Register #(.width(32)) A (.D(main_1_output), .en(ALoad), .Q(A_q), .clk(Clk));  // open: clr
  Register #(.width(32)) u_B (.D(main_1_output_2), .en(BLoad), .Q(B), .clk(Clk));  // open: clr
  Register #(.width(32)) imm_backup (.D(Imm), .en(imm_backup_ld), .Q(imm_backup_q), .clk(Clk));  // open: clr
  Multiplexer #(.width(32)) multiplexer_5 (.in0(PC_q), .in1(A_q), .out(multiplexer_5_out), .sel(ALUSrc1));  // open: en
  Multiplexer #(.select(2), .width(32)) multiplexer_6 (
    .in0(32'h4), .in1(B), .in2(imm_backup_q), .in3(32'hfffffffc), .out(multiplexer_6_out), .sel(ALUSrc2));  // open: en
  ALU alu_1 (
    .Input_1(multiplexer_5_out), .Input_2(multiplexer_6_out), .carry_in(Carry_In), .Op(SUB),
    .carry_out(Carry_Out), .select(OP), .Ouput(alu_1_ouput), .Zero(Zero));
  ALU alu_2 (
    .Input_1(32'h4), .Input_2(PC_q), .carry_in(1'b0), .Op(1'b0), .carry_out(alu_2_carry_out),
    .select(3'b000), .Ouput(alu_2_ouput));  // open: Zero
  Register #(.width(32)) u_ALUOut (.D(alu_1_ouput), .en(AluOutLd), .Q(ALUOut), .clk(memory_1_p8));  // open: clr
endmodule
