// Logisim project alutest.circ as structural Verilog: 2 circuits, main circuit main
module main (
  input  in_1,
  output bit0,
  output halt,
  output [31:0] out_4,
  output C,
  output Z
);

  wire clock_1_out;
  wire [7:0] opcode_munger_1_disp_2;
  wire [7:1] counter_1_q;
  wire [15:0] opcode_munger_1_disp;
  wire [31:0] bit_extender_1_out, bit_extender_2_out;

  Counter counter_1 (.Q({counter_1_q, bit0}), .carry(halt), .clk(clock_1_out));  // open: load, D, count, clr
  Clock clock_1 (.out(clock_1_out));
  Opcode_Munger opcode_munger_1 (
    .Opc({counter_1_q[2:1], bit0}), .disp({opcode_munger_1_disp_2, opcode_munger_1_disp}),
    .Sub(counter_1_q[7]));
  // Probe on counter_1_q[4:3]
  // Probe on counter_1_q[6:5]
  _7_Segment_Display u_7_segment_display_1 (
    .g(opcode_munger_1_disp[3]), .f(opcode_munger_1_disp[2]), .a(opcode_munger_1_disp[1]),
    .b(opcode_munger_1_disp[0]), .e(opcode_munger_1_disp[4]), .d(opcode_munger_1_disp[5]),
    .c(opcode_munger_1_disp[6]), .dp(opcode_munger_1_disp[7]));
  assign bit_extender_1_out = {{30{counter_1_q[4]}}, counter_1_q[4:3]};  // Bit_Extender bit_extender_1
  ALU alu_1 (
    .Input_1(bit_extender_1_out), .Input_2(bit_extender_2_out), .carry_in(in_1), .Op(counter_1_q[7]),
    .carry_out(C), .select({counter_1_q[2:1], bit0}), .Ouput(out_4), .Zero(Z));
  assign bit_extender_2_out = {{30{counter_1_q[6]}}, counter_1_q[6:5]};  // Bit_Extender bit_extender_2
  _7_Segment_Display u_7_segment_display_2 (
    .g(opcode_munger_1_disp[11]), .f(opcode_munger_1_disp[10]), .a(opcode_munger_1_disp[9]),
    .b(opcode_munger_1_disp[8]), .e(opcode_munger_1_disp[12]), .d(opcode_munger_1_disp[13]),
    .c(opcode_munger_1_disp[14]), .dp(opcode_munger_1_disp[15]));
  _7_Segment_Display u_7_segment_display_3 (
    .g(opcode_munger_1_disp_2[3]), .f(opcode_munger_1_disp_2[2]), .a(opcode_munger_1_disp_2[1]),
    .b(opcode_munger_1_disp_2[0]), .e(opcode_munger_1_disp_2[4]), .d(opcode_munger_1_disp_2[5]),
    .c(opcode_munger_1_disp_2[6]), .dp(opcode_munger_1_disp_2[7]));
endmodule

module Opcode_Munger (
  input  [2:0] Opc,
  input  Sub,
  output [23:0] disp
);

  wire [23:0] ADD_SUB, SR;

  Multiplexer #(.select(3), .width(24), .enable("false")) multiplexer_1 (
    .in0(ADD_SUB), .in1(24'h34346e), .in2(24'h43346e), .in3(24'hc3346e), .in4(24'hdf77dd), .in5(SR),
    .in6(24'hdf77), .in7(24'hf7575f), .out(disp), .sel(Opc));
  Multiplexer #(.width(24), .enable("false")) multiplexer_2 (
    .in0(24'hf7f75f), .in1(24'h7f756e), .out(ADD_SUB), .sel(Sub));
  Multiplexer #(.width(24), .enable("false")) multiplexer_3 (.in0(24'h34df6e), .in1(24'h5fdf6e), .out(SR), .sel(Sub));
endmodule
