// Logisim project cpu.circ as structural Verilog: 1 circuit, main circuit main
module main (
  input  C_in,
  input  Sub_in,
  output Carry_Out,
  output halt,
  output Zero
);

  wire clock_1_out, main_2_a_load, main_2_alu_out_ld, main_2_alu_src1, main_2_b_load, main_2_extend,
       main_2_i_or_d, main_2_ir_load, main_2_mdr_load, main_2_mem2reg, main_2_mem_read, main_2_mem_write,
       main_2_pc_load, main_2_pc_src, main_2_reg_src_2, main_2_reg_write, main_2_sub;
  wire [1:0] main_2_alu_src2, main_2_width;
  wire [2:0] main_2_alu_op;
  wire [4:0] main_2_rd, main_2_rs1, main_2_rs2;
  wire [31:0] main_1_aluout, main_1_inst, main_2_imm;

  data_path_main main_1 (
    .pcsrc(main_2_pc_src), .PCLoad(main_2_pc_load), .IOrD(main_2_i_or_d), .RegWrite(main_2_reg_write),
    .AluOutLd(main_2_alu_out_ld), .Rs2(main_2_rs2), .Rd(main_2_rd), .MemRd(main_2_mem_read),
    .MemWr(main_2_mem_write), .Imm(main_2_imm), .Width(main_2_width), .Extend(main_2_extend), .clear(1'b0),
    .Clk(clock_1_out), .ALoad(main_2_a_load), .BLoad(main_2_b_load), .MDRLoad(main_2_mdr_load),
    .IRLoad(main_2_ir_load), .Mem2Reg(main_2_mem2reg), .RegSrc2(main_2_reg_src_2), .Rs1(main_2_rs1),
    .ALUSrc1(main_2_alu_src1), .ALUSrc2(main_2_alu_src2), .Carry_In(1'b0), .SUB(main_2_sub),
    .OP(main_2_alu_op), .ALUOut(main_1_aluout), .Carry_Out(Carry_Out), .Zero(Zero), .inst(main_1_inst));
  Clock clock_1 (.out(clock_1_out));
  Fuad_s_Control_Unit_No_Nots_main main_2 (
    .ALU_Src1(main_2_alu_src1), .ALU_Src2(main_2_alu_src2), .alu_out(main_1_aluout), .PC_Src(main_2_pc_src),
    .ALU_Op(main_2_alu_op), .clk(clock_1_out), .Sub(main_2_sub), .I_Or_D(main_2_i_or_d),
    .Mem_Read(main_2_mem_read), .inst_in(main_1_inst), .IR_Load(main_2_ir_load), .imm(main_2_imm),
    .ALU_Out_Ld(main_2_alu_out_ld), .A_Load(main_2_a_load), .B_Load(main_2_b_load), .c_in(C_in),
    .rs1(main_2_rs1), .rs2(main_2_rs2), .z_in(Zero), .rd(main_2_rd), .Mem2Reg(main_2_mem2reg),
    .Reg_Write(main_2_reg_write), .Reg_Src_2(main_2_reg_src_2), .PC_Load(main_2_pc_load),
    .mdr_load(main_2_mdr_load), .Mem_Write(main_2_mem_write), .Sub_in(Sub_in), .Width(main_2_width),
    .extend(main_2_extend), .halt(halt));
endmodule
