// Logisim project multiplexer revised.circ as structural Verilog: 1 circuit, main circuit main
module main (
  input  [3:0] in_1,
  input  [3:0] in_2,
  input  [3:0] in_3,
  input  [3:0] in_4,
  input  [3:0] in_5,
  input  [3:0] in_6,
  input  [3:0] in_7,
  input  [2:0] in_8,
  input  [3:0] in_9,
  output [3:0] out_10
);

  Multiplexer #(.select(3)) multiplexer_1 (
    .in0(in_1[0]), .in1(in_2[0]), .in2(in_3[0]), .in3(in_4[0]), .in4(in_5[0]), .in5(in_6[0]), .in6(in_7[0]),
    .in7(in_9[0]), .out(out_10[0]), .sel(in_8));  // open: en
  Multiplexer #(.select(3)) multiplexer_2 (
    .in0(in_1[2]), .in1(in_2[2]), .in2(in_3[2]), .in3(in_4[2]), .in4(in_5[2]), .in5(in_6[2]), .in6(in_7[2]),
    .in7(in_9[2]), .out(out_10[2]), .sel(in_8));  // open: en
  Multiplexer #(.select(3)) multiplexer_3 (
    .in0(in_1[1]), .in1(in_2[1]), .in2(in_3[1]), .in3(in_4[1]), .in4(in_5[1]), .in5(in_6[1]), .in6(in_7[1]),
    .in7(in_9[1]), .out(out_10[1]), .sel(in_8));  // open: en
  Multiplexer #(.select(3)) multiplexer_4 (
    .in0(in_1[3]), .in1(in_2[3]), .in2(in_3[3]), .in3(in_4[3]), .in4(in_5[3]), .in5(in_6[3]), .in6(in_7[3]),
    .in7(in_9[3]), .out(out_10[3]), .sel(in_8));  // open: en

  // Other names for the same wires on the sheet: _0_0 = in_1[0]; _0_1 = in_1[1]; _0_2 = in_1[2]; _0_3 = in_1[3];
  //   _1_0 = in_2[0]; _1_1 = in_2[1]; _1_2 = in_2[2]; _1_3 = in_2[3]; _2_0 = in_3[0]; _2_1 = in_3[1]; _2_2 = in_3[2];
  //   _2_3 = in_3[3]; _3_0 = in_4[0]; _3_1 = in_4[1]; _3_2 = in_4[2]; _3_3 = in_4[3]; _4_0 = in_5[0]; _4_1 = in_5[1];
  //   _4_2 = in_5[2]; _4_3 = in_5[3]; _5_0 = in_6[0]; _5_1 = in_6[1]; _5_2 = in_6[2]; _5_3 = in_6[3]; _6_0 = in_7[0];
  //   _6_1 = in_7[1]; _6_2 = in_7[2]; _6_3 = in_7[3]; _7_0 = in_9[0]; _7_1 = in_9[1]; _7_2 = in_9[2]; _7_3 = in_9[3]
endmodule
