// Logisim project my own Adder.circ as structural Verilog: 1 circuit, main circuit adder
module adder (
  input  carry,
  input  [31:0] Input_1,
  input  Select,
  input  [31:0] Input_2,
  output overflow,
  output [31:0] \output 
);

  wire adder_1_cout, and_1_out, and_2_out, subtractor_1_bout;
  wire [31:0] adder_1_out, subtractor_1_out;

  Subtractor #(.width(32)) subtractor_1 (
    .a(Input_1), .b(Input_2), .out(subtractor_1_out), .bin(carry), .bout(subtractor_1_bout));
  Adder #(.width(32)) adder_1 (.a(Input_1), .b(Input_2), .out(adder_1_out), .cin(carry), .cout(adder_1_cout));
  and and_1 (and_1_out, subtractor_1_bout, Select);
  Multiplexer #(.width(32), .enable("false")) multiplexer_1 (
    .in0(adder_1_out), .in1(subtractor_1_out), .out(\output ), .sel(Select));
  or or_1 (overflow, and_2_out, and_1_out);
  and and_2 (and_2_out, ~Select, adder_1_cout);  // AND_Gate
endmodule
