// Logisim project set less than.circ as structural Verilog: 1 circuit, main circuit slt
module slt (
  input  carry_in,
  input  [31:0] input_1,
  input  [31:0] input_2,
  output [31:0] \output ,
  output carry_out
);

  wire and_1_out, and_2_out, and_3_out, and_4_out, and_5_out, and_6_out, and_7_out, and_8_out, not_1_out,
       not_2_out, not_3_out, or_1_out, xor_1_out;
  wire [31:0] subtractor_1_out;

  and and_1 (and_1_out, ~input_1[0], ~input_1[1], ~input_1[2], ~input_1[3], ~input_1[4], ~input_1[5], ~input_1[6], ~input_1[7], ~input_1[8], ~input_1[9], ~input_1[10], ~input_1[11], ~input_1[12], ~input_1[13], ~input_1[14], ~input_1[15], ~input_1[16], ~input_1[17], ~input_1[18], ~input_1[19], ~input_1[20], ~input_1[21], ~input_1[22], ~input_1[23], ~input_1[24], ~input_1[25], ~input_1[26], ~input_1[27], ~input_1[28], ~input_1[29], ~input_1[30]);  // AND_Gate
  and and_2 (and_2_out, ~input_2[0], ~input_2[1], ~input_2[2], ~input_2[3], ~input_2[4], ~input_2[5], ~input_2[6], ~input_2[7], ~input_2[8], ~input_2[9], ~input_2[10], ~input_2[11], ~input_2[12], ~input_2[13], ~input_2[14], ~input_2[15], ~input_2[16], ~input_2[17], ~input_2[18], ~input_2[19], ~input_2[20], ~input_2[21], ~input_2[22], ~input_2[23], ~input_2[24], ~input_2[25], ~input_2[26], ~input_2[27], ~input_2[28], ~input_2[29], ~input_2[30]);  // AND_Gate
  Subtractor #(.width(32)) subtractor_1 (
    .a(input_1), .b(input_2), .out(subtractor_1_out), .bin(carry_in), .bout(carry_out));
  and and_3 (and_3_out, input_1[31], input_2[31]);
  and and_4 (and_4_out, input_2[31], input_1[31]);
  xor xor_1 (xor_1_out, and_3_out, subtractor_1_out[31]);
  and and_5 (and_5_out, and_4_out, and_1_out, and_2_out);
  not not_1 (not_1_out, input_2[31]);
  and and_6 (and_6_out, input_1[31], not_1_out);
  not not_2 (not_2_out, input_1[31]);
  or or_1 (or_1_out, xor_1_out, and_6_out);
  and and_7 (and_7_out, not_2_out, input_2[31]);
  not not_3 (not_3_out, and_7_out);
  and and_8 (and_8_out, or_1_out, ~and_5_out, not_3_out);  // AND_Gate
  assign \output  = {{31{1'b0}}, and_8_out};  // Bit_Extender bit_extender_1
endmodule
